# Fritzing sketch Bootloader (saved by Fritzing 0.9.1b)
circuit board: 6.5848cm x 5.09976cm

parts:
  R1 = Resistor [tolerance=±5% resistance=10k package=THT]
  J6 = female pin header, 4 pins [form="♀ (female)"]
  J7 = female pin header, 14 pins [form="♀ (female)"]
  C3 = Electrolytic Capacitor [capacitance=10µF package="100 mil [THT, electrolytic]"]
  S3 = Pushbutton [package="[THT]"]
  Green1 = LED - 3mm [color="Green (555nm)" package="3 mm [THT]"]
  Yellow1 = LED - 3mm [color="Yellow (585nm)" package="3 mm [THT]"]
  Red1 = LED - 3mm [color="Red (633nm)" package="3 mm [THT]"]
  R4 = Resistor [tolerance=±1% resistance=220 package=THT]
  R5 = Resistor [tolerance=±1% resistance=220 package=THT]
  R6 = Resistor [tolerance=±1% resistance=2.2k package=THT]
  J8 = female pin header, 14 pins [form="♀ (female)"]
  J9 = female pin header, 3 pins [form="♀ (female)"]
  J10 = female pin header, 8 pins [form="♀ (female)"]
  U2 = atmega168 [package=dip]

nets:
  N1: R1.Pin_0, J6.pin3, J7.pin8, J7.pin9, J8.pin7, U2.VCC, U2.AVCC, U2.AREF
  N2: R1.Pin_1, S3.Pin_3, S3.Pin_4, J8.pin1, J10.pin5, U2.RESET
  N3: J6.pin1, C3.+
  GND: J6.pin4, J7.pin7, C3.-, S3.Pin_1, S3.Pin_2, Green1.cathode, Yellow1.cathode, Red1.cathode, J8.pin8, J9.pin2, J10.pin1, U2.GND
  N4: J7.pin1, U2.A5
  N5: J7.pin2, U2.A4
  N6: J7.pin3, U2.A3
  N7: J7.pin4, U2.A2
  N8: J7.pin5, U2.A1
  N9: J7.pin6, U2.A0
  N10: J7.pin10, J10.pin2, U2.D13
  N11: J7.pin11, J10.pin3, U2.D12
  N12: J7.pin12, J10.pin4, U2.D11_(PWM)
  N13: J7.pin13, U2.D10_(PWM)
  N14: J7.pin14, U2.D9_(PWM)
  N15: Green1.anode, R6.Pin_1
  N16: Yellow1.anode, R4.Pin_1
  N17: Red1.anode, R5.Pin_0
  N18: R4.Pin_0, J10.pin6
  N19: R5.Pin_1, J10.pin7
  N20: R6.Pin_0, J10.pin8
  N21: J8.pin2, U2.D0_(RX)
  N22: J8.pin3, U2.D1_(TX)
  N23: J8.pin4, U2.D2
  N24: J8.pin5, U2.D3_(PWM)
  N25: J8.pin6, U2.D4
  N26: J8.pin9, J9.pin1, U2.XLAT1
  N27: J8.pin10, J9.pin3, U2.XLAT2
  N28: J8.pin11, U2.D5_(PWM)
  N29: J8.pin12, U2.D6_(PWM)
  N30: J8.pin13, U2.D7
  N31: J8.pin14, U2.D8
