# Fritzing sketch AtTiny programmer (saved by Fritzing 0.9.1b)
circuit board: 8.42723cm x 6.49515cm
breadboards: 1

parts:
  R1 = Resistor [tolerance=±5% resistance=220 package=THT]
  R2 = Resistor [tolerance=±5% resistance=220 package=THT]
  U1 = attiny85 [package=dip]
  LED3 = LED - 5mm [color="Red (633nm)" package="5 mm [THT]"]
  LED4 = LED - 5mm [color="Yellow (595nm)" package="5 mm [THT]"]
  LED5 = LED - 5mm [color="Green (555nm)" package="5 mm [THT]"]
  R4 = Resistor [tolerance=±5% resistance=220 package=THT]
  R5 = Resistor [tolerance=±5% resistance=220 package=THT]
  R3 = Resistor [tolerance=±5% resistance=220 package=THT]
  LED6 = LED - 5mm [color="Blue (525nm)" package="5 mm [THT]"]
  J1 = female pin header, 3 pins [form="♀ (female)"]
  J2 = female pin header, 3 pins [form="♀ (female)"]
  J3 = female pin header, 5 pins [form="♀ (female)"]
  J4 = female pin header, 6 pins [form="♀ (female)"]
  J5 = female pin header, 1 pin [form="♀ (female)"]
  C1 = Electrolytic Capacitor [capacitance=10µF voltage=10V package="100 mil [THT, electrolytic]"]

nets:
  N1: R1.Pin_0, J5.pin1
  N2: R1.Pin_1, LED3.anode
  N3: R2.Pin_0, J4.pin6
  N4: R2.Pin_1, LED5.anode
  N5: U1.Pin_1, J4.pin4
  N6: U1.Pin_2, LED6.anode
  N7: U1.Pin_3, R5.Pin_1, J1.pin3, J2.pin3
  N8: U1.Pin_4, LED3.cathode, LED4.cathode, LED5.cathode, R4.Pin_0, J1.pin1, J2.pin1, J3.pin4, J3.pin5, C1.-
  N9: U1.Pin_5, J4.pin3
  N10: U1.Pin_6, J4.pin2
  N11: U1.Pin_7, J4.pin1
  N12: U1.Pin_8, R5.Pin_0, J3.pin3
  N13: LED4.anode, R3.Pin_0
  N14: R4.Pin_1, LED6.cathode
  N15: R3.Pin_1, J4.pin5
  N16: J3.pin1, C1.+
