# Fritzing sketch pcb (saved by Fritzing 0.9.1b)
circuit board: 2.31218cm x 4.03744cm
breadboards: 1

parts:
  U1 = MAX7219 [package=dil24]
  U2 = 7-SEGMENT-4DIGIT [package=7-segment-4digit]
  U3 = attiny85 [package=dip]
  J1 = female pin header, 2 pins [form="♀ (female)"]
  J2 = female pin header, 2 pins [form="♀ (female)"]
  R1 = Resistor [tolerance=±5% resistance=30k package="0805 [SMD]"]

nets:
  N1: U1.DIN, U3.Pin_7
  N2: U1.DIG0, U2.1
  N3: U1.DIG4, U2.4
  GND: U1.GND, U1.GND2, U3.Pin_4, J2.pin2
  N4: U1.DIG2, U2.6
  N5: U1.DIG3, U2.8
  N6: U1.DIG1, U2.2
  N7: U1.LOAD, U3.Pin_6
  N8: U1.CLK, U3.Pin_5
  N9: U1.SEGA, U2.14
  N10: U1.SEGF, U2.11
  N11: U1.SEGB, U2.16
  N12: U1.SEGG, U2.15
  N13: U1.ISET, R1.Pin_1
  5V: U1.VCC, U3.Pin_8, J2.pin1, R1.Pin_0
  N14: U1.SEGC, U2.13
  N15: U1.SEGE, U2.5
  N16: U1.SEGDP, U2.7
  N17: U1.SEGD, U2.3
  N18: U3.Pin_2, J1.pin1
  N19: U3.Pin_3, J1.pin2
