# Fritzing sketch capacidance meter (saved by Fritzing 0.9.1b)
circuit board: 5.41cm x 5.05cm

parts:
  R1 = Resistor [tolerance=±5% resistance=10k package=THT]
  R2 = Resistor [tolerance=±5% resistance=220 package=THT]
  R4 = Resistor [tolerance=±5% resistance=220 package=THT]
  XTAL1 = Crystal [frequency="16 Mhz" package=THT]
  C2 = Ceramic Capacitor [capacitance=100nF package="100 mil [THT, multilayer]"]
  C3 = Ceramic Capacitor [capacitance=100nF package="100 mil [THT, multilayer]"]
  R5 = Trimmer Potentiometer [maximum_resistance=10kΩ package=THT]
  U1 = atmega328 [package=dip]
  J1 = female pin header, 16 pins [form="♀ (female)"]
  R6 = Resistor [tolerance=±5% resistance=10k package=THT]
  R16 = Resistor [tolerance=±5% resistance=1M package=THT]
  R15 = Resistor [tolerance=±5% resistance=100k package=THT]
  R14 = Resistor [tolerance=±5% resistance=1k package=THT]
  U2 = Voltage Regulator - 5V [package="TO220 [THT]"]
  S1 = Toggle Switch [package=THT]
  J6 = female pin header, 3 pins [form="♀ (female)"]
  J7 = female pin header, 3 pins [form="♀ (female)"]
  R17 = Resistor [tolerance=±5% resistance=10k package=THT]
  J5 = female pin header, 2 pins [form="♀ (female)"]
  LCD1 = LCD screen  # not connected
  R18 = Resistor [tolerance=±5% resistance=10m package=THT]
  Pad1 = Pad [width=26 height=50 connect=center]  # not connected
  J4 = double row female pin header, 12 pins [form="♀ (female)"]

nets:
  N1: R1.Pin_0, R2.Pin_0, U1.A0, R16.Pin_1, R15.Pin_1, R14.Pin_1, R18.Pin_1, J4.pin1, J4.pin2, J4.pin3, J4.pin4, J4.pin5, J4.pin6
  N2: R1.Pin_1, U1.D10_(PWM)
  N3: R2.Pin_1, U1.D7
  GND: R4.Pin_0, C2.0, C3.0, R5.leg2, U1.GND, J1.pin12, J1.pin16, U2.GND, R17.Pin_1, J5.pin2, J4.pin7, J4.pin8, J4.pin9, J4.pin10, J4.pin11, J4.pin12
  N4: R4.Pin_1, J1.pin1
  N5: XTAL1.pin_0, C2.1, U1.XLAT1
  N6: XTAL1.pin_1, C3.1, U1.XLAT2
  5V: R5.leg1, U1.VCC, U1.AVCC, U1.AREF, J1.pin2, J1.pin15, R6.Pin_1, U2.output_voltage, J6.pin1, J7.pin1
  N7: R5.wiper, J1.pin14
  N8: U1.RESET, R6.Pin_0
  N9: U1.D2, J1.pin3
  N10: U1.D3_(PWM), J1.pin4
  N11: U1.D4, J1.pin5
  N12: U1.D5_(PWM), J1.pin6
  N13: U1.D6_(PWM), J1.pin11
  N14: U1.D8, J1.pin13
  N15: U1.D9_(PWM), R14.Pin_0
  N16: U1.D11_(PWM), R15.Pin_0
  N17: U1.D12, R16.Pin_0
  N18: U1.D13, R18.Pin_0
  N19: U1.A1, J6.pin3, J7.pin3, R17.Pin_0
  N20: U2.input_voltage, S1.L2
  N21: S1.COM, J5.pin1
