# Fritzing sketch 2 (saved by Fritzing 0.9.1b)
circuit board: 8.46667cm x 5.64444cm
breadboards: 1

parts:
  J1 = Basic Servo
  U1 = atmega328 [package=dip]
  XTAL1 = Crystal [frequency="16 Mhz" package=THT]
  C1 = Ceramic Capacitor [capacitance=22p package="100 mil [THT, multilayer]"]
  C2 = Ceramic Capacitor [capacitance=22p package="100 mil [THT, multilayer]"]
  J2 = female pin header, 6 pins [form="♀ (female)"]

nets:
  GND: J1.gnd, U1.GND, C1.0, C2.0, J2.pin6
  5V: J1.vcc, U1.VCC, U1.AVCC, U1.AREF, J2.pin5
  N1: J1.pulse, U1.D3_(PWM)
  N2: U1.D0_(RX), J2.pin2
  N3: U1.D1_(TX), J2.pin3
  N4: U1.D2, J2.pin4
  N5: U1.XLAT1, XTAL1.pin_1, C1.1
  N6: U1.XLAT2, XTAL1.pin_0, C2.1
  N7: U1.A1, J2.pin1
