# Fritzing sketch colorsensor (saved by Fritzing 0.9.1b)
circuit board: 2.70978cm x 1.7203cm
breadboards: 1

parts:
  R5 = Resistor [tolerance=±5% resistance=100k package=THT]
  J2 = female pin header, 4 pins [form="♀ (female)"]
  J3 = female pin header, 2 pins [form="♀ (female)"]
  J1 = female pin header, 6 pins [form="♀ (female)"]

nets:
  N1: R5.Pin_0, J3.pin1, J1.pin1
  N2: R5.Pin_1, J2.pin2, J1.pin5
  N3: J2.pin1, J1.pin4
  N4: J2.pin3, J1.pin3
  N5: J2.pin4, J1.pin2
  N6: J3.pin2, J1.pin6
