# Fritzing sketch diy arduino powerboards v1 (saved by Fritzing 0.9.1b)
circuit board: 1.58164cm x 3.61629cm
breadboards: 1

parts:
  J1 = female pin header, 3 pins [form="♀ (female)"]
  J2 = female pin header, 4 pins [form="♀ (female)"]
  J3 = male pin header, 2 pins [form="♂ (male)"]
  XTAL1 = Crystal [frequency="16 Mhz" package=THT]
  C1 = Ceramic Capacitor [capacitance=22nF package="100 mil [THT, multilayer]"]
  C2 = Ceramic Capacitor [capacitance=22nF package="100 mil [THT, multilayer]"]
  R5 = Resistor [tolerance=±5% resistance=10k package=THT]
  U1 = atmega168 [package=dip]  # not connected
  U2 = Voltage Regulator - 5V [package="TO220 [THT]"]
  J4 = female pin header, 2 pins [form="♀ (female)"]
  J5 = male pin header, 2 pins [form="♂ (male)"]
  C3 = Ceramic Capacitor [capacitance=33nF package="100 mil [THT, multilayer]"]
  C4 = Ceramic Capacitor [capacitance=100nF package="100 mil [THT, multilayer]"]
  LED1 = LED - 3mm [color="Green (555nm)" package="3 mm [THT]"]
  R6 = Resistor [tolerance=±5% resistance=220 package=THT]
  J6 = female pin header, 3 pins [form="♀ (female)"]
  J7 = female pin header, 3 pins [form="♀ (female)"]

nets:
  N1: J1.pin1, J2.pin2, J3.pin2, C1.1, C2.1, J6.pin3, J7.pin3
  N2: J1.pin2, J2.pin1, J3.pin1, R5.Pin_1
  N3: J1.pin3, R5.Pin_0, J6.pin1, J7.pin1
  N4: J2.pin3, XTAL1.pin_1, C1.0
  N5: J2.pin4, XTAL1.pin_0, C2.0
  N6: U2.input_voltage, J5.pin2, C4.1
  N7: U2.GND, J4.pin2, J5.pin1, C3.1, C4.0, LED1.cathode
  N8: U2.output_voltage, J4.pin1, C3.0, R6.Pin_0
  N9: LED1.anode, R6.Pin_1
