# Fritzing sketch diy arduino v1 (saved by Fritzing 0.9.0b)
circuit board: 4.55448cm x 3.80756cm
breadboards: 1

parts:
  U1 = atmega328 [package=dip]
  C1 = Ceramic Capacitor [capacitance=22pF package="100 mil [THT, multilayer]"]
  C2 = Ceramic Capacitor [capacitance=22pF package="100 mil [THT, multilayer]"]
  J2 = female pin header, 6 pins [form="♀ (female)"]
  J1 = female pin header, 14 pins [form="♀ (female)"]
  R4 = Resistor [tolerance=±5% resistance=220 package=THT]
  R5 = Resistor [tolerance=±5% resistance=220 package=THT]
  LED4 = LED - 3mm [color="Yellow (595nm)" package="3 mm [THT]"]
  LED3 = LED - 3mm [color="Green (560nm)" package="3 mm [THT]"]
  J3 = female pin header, 3 pins [form="♀ (female)"]
  XTAL1 = Crystal [frequency="16 Mhz" package=THT]

nets:
  N1: U1.RESET, J3.pin2
  N2: U1.D0_(RX), J1.pin1, LED4.anode
  N3: U1.D1_(TX), J1.pin2, LED3.anode
  N4: U1.D2, J1.pin3
  N5: U1.D3_(PWM), J1.pin4
  N6: U1.D4, J1.pin5
  N7: U1.VCC, U1.AVCC, U1.AREF, J3.pin1
  N8: U1.GND, C1.1, C2.1, R4.Pin_1, R5.Pin_1, J3.pin3
  N9: U1.XLAT1, C2.0, XTAL1.pin_0
  N10: U1.XLAT2, C1.0, XTAL1.pin_1
  N11: U1.D5_(PWM), J1.pin6
  N12: U1.D6_(PWM), J1.pin7
  N13: U1.D7, J1.pin8
  N14: U1.D8, J1.pin9
  N15: U1.D9_(PWM), J1.pin10
  N16: U1.D10_(PWM), J1.pin11
  N17: U1.D11_(PWM), J1.pin12
  N18: U1.D12, J1.pin13
  N19: U1.D13, J1.pin14
  N20: U1.A0, J2.pin1
  N21: U1.A1, J2.pin2
  N22: U1.A2, J2.pin3
  N23: U1.A3, J2.pin4
  N24: U1.A4, J2.pin5
  N25: U1.A5, J2.pin6
  N26: R4.Pin_0, LED3.cathode
  N27: R5.Pin_0, LED4.cathode
