# Fritzing sketch diy arduino v2 (saved by Fritzing 0.9.1b)
circuit board: 4.62358cm x 3.05711cm
breadboards: 1

parts:
  U1 = atmega328 [package=dip]
  C1 = Ceramic Capacitor [capacitance=22pF package="100 mil [THT, multilayer]"]
  C2 = Ceramic Capacitor [capacitance=22pF package="100 mil [THT, multilayer]"]
  J2 = female pin header, 6 pins [form="♀ (female)"]
  R4 = Resistor [tolerance=±5% resistance=220 package=THT]
  R5 = Resistor [tolerance=±5% resistance=220 package=THT]
  LED4 = LED - 3mm [color="Yellow (595nm)" package="3 mm [THT]"]
  LED3 = LED - 3mm [color="Green (560nm)" package="3 mm [THT]"]
  J3 = female pin header, 3 pins [form="♀ (female)"]
  XTAL1 = Crystal [frequency="16 Mhz" package=THT]
  J4 = female pin header, 9 pins [form="♀ (female)"]
  J5 = female pin header, 5 pins [form="♀ (female)"]

nets:
  N1: U1.RESET, J3.pin2
  N2: U1.D0_(RX), LED4.anode, J5.pin1
  N3: U1.D1_(TX), LED3.anode, J5.pin2
  N4: U1.D2, J5.pin3
  N5: U1.D3_(PWM), J5.pin4
  N6: U1.D4, J5.pin5
  N7: U1.VCC, U1.AVCC, U1.AREF, J3.pin1
  N8: U1.GND, C1.1, C2.1, R4.Pin_1, R5.Pin_1, J3.pin3
  N9: U1.XLAT1, C2.0, XTAL1.pin_0
  N10: U1.XLAT2, C1.0, XTAL1.pin_1
  N11: U1.D5_(PWM), J4.pin1
  N12: U1.D6_(PWM), J4.pin2
  N13: U1.D7, J4.pin3
  N14: U1.D8, J4.pin4
  N15: U1.D9_(PWM), J4.pin5
  N16: U1.D10_(PWM), J4.pin6
  N17: U1.D11_(PWM), J4.pin7
  N18: U1.D12, J4.pin8
  N19: U1.D13, J4.pin9
  N20: U1.A0, J2.pin1
  N21: U1.A1, J2.pin2
  N22: U1.A2, J2.pin3
  N23: U1.A3, J2.pin4
  N24: U1.A4, J2.pin5
  N25: U1.A5, J2.pin6
  N26: R4.Pin_0, LED3.cathode
  N27: R5.Pin_0, LED4.cathode
