# Fritzing sketch diy arduino v3 (saved by Fritzing 0.9.1b)
circuit board: 3.6264cm x 1.59426cm
breadboards: 1

parts:
  J2 = female pin header, 6 pins [form="♀ (female)"]
  J3 = female pin header, 3 pins [form="♀ (female)"]
  J4 = female pin header, 4 pins [form="♀ (female)"]
  J6 = female pin header, 5 pins [form="♀ (female)"]
  J7 = female pin header, 4 pins [form="♀ (female)"]
  U1 = atmega328 [package=dip]
  J8 = female pin header, 6 pins [form="♀ (female)"]

nets:
  N1: J2.pin1, U1.A0
  N2: J2.pin2, U1.A1
  N3: J2.pin3, U1.A2
  N4: J2.pin4, U1.A3
  N5: J2.pin5, U1.A4
  N6: J2.pin6, U1.A5
  N7: J3.pin1, U1.RESET, J8.pin1
  N8: J3.pin2, U1.AVCC, U1.AREF
  N9: J3.pin3, J7.pin2, U1.GND
  N10: J4.pin1, U1.D5_(PWM)
  N11: J4.pin2, U1.D6_(PWM)
  N12: J4.pin3, U1.D7
  N13: J4.pin4, U1.D8
  N14: J6.pin1, U1.D13
  N15: J6.pin2, U1.D12
  N16: J6.pin3, U1.D11_(PWM)
  N17: J6.pin4, U1.D10_(PWM)
  N18: J6.pin5, U1.D9_(PWM)
  N19: J7.pin1, U1.VCC
  N20: J7.pin3, U1.XLAT1
  N21: J7.pin4, U1.XLAT2
  N22: U1.D0_(RX), J8.pin2
  N23: U1.D1_(TX), J8.pin3
  N24: U1.D2, J8.pin4
  N25: U1.D3_(PWM), J8.pin5
  N26: U1.D4, J8.pin6
