# Fritzing sketch rgbled Photon (saved by Fritzing 0.9.1b)
circuit board: 5.3cm x 3.1cm
breadboards: 1

parts:
  Q1 = Basic FET N-Channel [package="TO220 [THT]"]
  Q3 = Basic FET N-Channel [package="TO220 [THT]"]
  Q4 = Basic FET N-Channel [package="TO220 [THT]"]
  Q5 = Basic FET N-Channel [package="TO220 [THT]"]
  Q6 = Basic FET N-Channel [package="TO220 [THT]"]
  Q2 = Basic FET N-Channel [package="TO220 [THT]"]
  U2 = Voltage Regulator - 3.3V [package="TO220 [THT]"]
  Part2 = Photon
  J3 = female pin header, 2 pins [form="♀ (female)"]
  J4 = female pin header, 4 pins [form="♀ (female)"]
  J2 = female pin header, 4 pins [form="♀ (female)"]

nets:
  N1: Q1.gate, Part2.A4
  GND: Q1.drain, Q3.drain, Q4.drain, Q5.drain, Q6.drain, Q2.drain, U2.GND, Part2.GND, J3.pin2
  N2: Q1.source, J2.pin1
  N3: Q3.gate, Part2.D0
  N4: Q3.source, J2.pin3
  N5: Q4.gate, Part2.WKP
  N6: Q4.source, J4.pin4
  N7: Q5.gate, Part2.RX
  N8: Q5.source, J4.pin3
  N9: Q6.gate, Part2.TX
  N10: Q6.source, J4.pin2
  N11: Q2.gate, Part2.A5
  N12: Q2.source, J2.pin2
  12V: U2.input_voltage, J3.pin1, J4.pin1, J2.pin4
  N13: U2.output_voltage, Part2.3V3
