# Fritzing sketch rgbled copy (saved by Fritzing 0.9.1b)
circuit board: 4.89627cm x 3.88989cm
breadboards: 1

parts:
  R1 = Resistor [tolerance=±5% resistance=10k package=THT]
  C1 = Ceramic Capacitor [capacitance=100nF package="100 mil [THT, multilayer]"]
  C2 = Ceramic Capacitor [capacitance=100nF package="100 mil [THT, multilayer]"]
  Q1 = Basic FET N-Channel [package="TO220 [THT]"]
  Q2 = Basic FET N-Channel [package="TO220 [THT]"]
  Q3 = Basic FET N-Channel [package="TO220 [THT]"]
  J1 = female pin header, 3 pins [form="♀ (female)"]
  J2 = female pin header, 4 pins [form="♀ (female)"]
  U1 = atmega328 [package=dip]
  J3 = female pin header, 2 pins [form="♀ (female)"]
  XTAL1 = Crystal [frequency="16 Mhz" package=THT]
  Q4 = Basic FET N-Channel [package="TO220 [THT]"]
  Q5 = Basic FET N-Channel [package="TO220 [THT]"]
  Q6 = Basic FET N-Channel [package="TO220 [THT]"]
  J4 = female pin header, 4 pins [form="♀ (female)"]
  U2 = Voltage Regulator - 5V [package="TO220 [THT]"]

nets:
  N1: R1.Pin_0, U1.RESET
  N2: R1.Pin_1, J1.pin1, U1.VCC, U1.AVCC, U1.AREF, U2.output_voltage
  N3: C1.0, U1.XLAT2, XTAL1.pin_1
  GND: C1.1, C2.1, Q1.drain, Q2.drain, Q3.drain, J1.pin2, U1.GND, J3.pin2, Q4.drain, Q5.drain, Q6.drain, U2.GND
  N4: C2.0, U1.XLAT1, XTAL1.pin_0
  N5: Q1.gate, U1.D6_(PWM)
  N6: Q1.source, J2.pin4
  N7: Q2.gate, U1.D5_(PWM)
  N8: Q2.source, J2.pin3
  N9: Q3.gate, U1.D3_(PWM)
  N10: Q3.source, J2.pin2
  N11: J1.pin3, U1.D4
  12V: J2.pin1, J3.pin1, J4.pin1, U2.input_voltage
  N12: U1.D9_(PWM), Q4.gate
  N13: U1.D10_(PWM), Q5.gate
  N14: U1.D11_(PWM), Q6.gate
  N15: Q4.source, J4.pin4
  N16: Q5.source, J4.pin3
  N17: Q6.source, J4.pin2
