# Fritzing sketch rgbled sparkcore (saved by Fritzing 0.9.1b)
circuit board: 6.1277cm x 3.07803cm
breadboards: 1

parts:
  Q1 = Basic FET N-Channel [package="TO220 [THT]"]
  Q3 = Basic FET N-Channel [package="TO220 [THT]"]
  J1 = female pin header, 3 pins [form="♀ (female)"]
  J2 = female pin header, 4 pins [form="♀ (female)"]
  J3 = female pin header, 2 pins [form="♀ (female)"]
  Q4 = Basic FET N-Channel [package="TO220 [THT]"]
  Q5 = Basic FET N-Channel [package="TO220 [THT]"]
  Q6 = Basic FET N-Channel [package="TO220 [THT]"]
  J4 = female pin header, 4 pins [form="♀ (female)"]
  U2 = Voltage Regulator - 5V [package="TO220 [THT]"]
  Part1 = Spark Core (v1.0)
  Q2 = Basic FET N-Channel [package="TO220 [THT]"]
  Part2 = Spark Core (v1.0)  # not connected

nets:
  N1: Q1.gate, Part1.A4
  GND: Q1.drain, Q3.drain, J1.pin2, J3.pin2, Q4.drain, Q5.drain, Q6.drain, U2.GND, Part1.GND, Q2.drain
  N2: Q1.source, J2.pin1
  N3: Q3.gate, Part1.A1
  N4: Q3.source, J2.pin3
  12V: J1.pin1, U2.input_voltage, Part1.3V3
  N5: J1.pin3, Part1.D6
  N6: J2.pin2, Q2.source
  N7: J2.pin4, J3.pin1, J4.pin1, U2.output_voltage
  N8: Q4.gate, Part1.A5
  N9: Q4.source, J4.pin4
  N10: Q5.gate, Part1.A6
  N11: Q5.source, J4.pin3
  N12: Q6.gate, Part1.A7
  N13: Q6.source, J4.pin2
  N14: Part1.A0, Q2.gate
