# Fritzing sketch v1 (saved by Fritzing 0.9.1b)
circuit board: 1.06514cm x 2.32572cm
circuit board: 3.07427cm x 5.35089cm
breadboards: 1

parts:
  XTAL1 = Crystal [frequency="16 Mhz" package=THT]
  C1 = Ceramic Capacitor [capacitance=100nF package="100 mil [THT, multilayer]"]
  C2 = Ceramic Capacitor [capacitance=100nF package="100 mil [THT, multilayer]"]
  J11 = female pin header, 3 pins [form="♀ (female)"]
  J12 = female pin header, 3 pins [form="♀ (female)"]
  J13 = female pin header, 3 pins [form="♀ (female)"]
  J14 = female pin header, 3 pins [form="♀ (female)"]
  J15 = female pin header, 3 pins [form="♀ (female)"]
  J16 = female pin header, 3 pins [form="♀ (female)"]
  J18 = female pin header, 3 pins [form="♀ (female)"]
  J21 = female pin header, 2 pins [form="♀ (female)"]
  J22 = female pin header, 2 pins [form="♀ (female)"]
  J23 = female pin header, 2 pins [form="♀ (female)"]
  J24 = female pin header, 2 pins [form="♀ (female)"]
  J25 = female pin header, 2 pins [form="♀ (female)"]
  J26 = female pin header, 2 pins [form="♀ (female)"]
  J27 = female pin header, 2 pins [form="♀ (female)"]
  J28 = female pin header, 2 pins [form="♀ (female)"]
  J29 = female pin header, 3 pins [form="♀ (female)"]
  J30 = female pin header, 3 pins [form="♀ (female)"]
  J31 = female pin header, 3 pins [form="♀ (female)"]
  J32 = female pin header, 2 pins [form="♀ (female)"]
  J33 = female pin header, 3 pins [form="♀ (female)"]
  J34 = female pin header, 2 pins [form="♀ (female)"]
  J35 = female pin header, 2 pins [form="♀ (female)"]
  J37 = female pin header, 2 pins [form="♀ (female)"]
  J38 = female pin header, 5 pins [form="♀ (female)"]
  Q2 = NPN-Transistor [package="TO92 [THT]"]
  U1 = atmega328 [package=dip]
  Q9 = NPN-Transistor [package="TO92 [THT]"]
  Q3 = NPN-Transistor [package="TO92 [THT]"]
  Q4 = NPN-Transistor [package="TO92 [THT]"]
  Q5 = NPN-Transistor [package="TO92 [THT]"]
  Q6 = NPN-Transistor [package="TO92 [THT]"]
  Q7 = NPN-Transistor [package="TO92 [THT]"]
  Q8 = NPN-Transistor [package="TO92 [THT]"]
  R3 = Resistor [tolerance=±5% resistance=220 package=THT]
  R10 = Resistor [tolerance=±5% resistance=220 package=THT]
  R9 = Resistor [tolerance=±5% resistance=220 package=THT]
  R8 = Resistor [tolerance=±5% resistance=220 package=THT]
  R7 = Resistor [tolerance=±5% resistance=220 package=THT]
  R6 = Resistor [tolerance=±5% resistance=220 package=THT]
  R5 = Resistor [tolerance=±5% resistance=220 package=THT]
  R4 = Resistor [tolerance=±5% resistance=220 package=THT]
  J39 = female pin header, 2 pins [form="♀ (female)"]
  J40 = female pin header, 2 pins [form="♀ (female)"]

nets:
  N1: XTAL1.pin_0, C1.0, U1.XLAT2
  N2: XTAL1.pin_1, C2.0, U1.XLAT1
  N3: C1.1, C2.1, J11.pin3, J12.pin3, J13.pin3, J14.pin3, J15.pin3, J16.pin3, J34.pin2, J38.pin5, Q2.E, U1.GND, Q9.E, Q3.E, Q4.E, Q5.E, Q6.E, Q7.E, Q8.E, J39.pin2, J40.pin2
  N4: J11.pin1, J12.pin1, J31.pin3, J38.pin3, U1.D4
  N5: J13.pin1, J14.pin1, J31.pin2, J38.pin2, U1.D3_(PWM)
  N6: J15.pin1, J16.pin1, J31.pin1, J38.pin1, U1.D2
  N7: J18.pin1, U1.RESET
  N8: J18.pin2, U1.D0_(RX)
  N9: J18.pin3, U1.D1_(TX)
  N10: J21.pin1, J22.pin1, J23.pin1, J24.pin1, J25.pin1, J26.pin1, J27.pin1, J34.pin1, J35.pin1, U1.VCC, U1.AVCC, U1.AREF, J39.pin1, J40.pin1
  N11: J21.pin2, R6.Pin_1
  N12: J22.pin2, R3.Pin_1
  N13: J23.pin2, R4.Pin_1
  N14: J24.pin2, R5.Pin_1
  N15: J25.pin2, R9.Pin_1
  N16: J26.pin2, R8.Pin_1
  N17: J27.pin2, R7.Pin_1
  N18: J28.pin1, U1.D5_(PWM)
  N19: J28.pin2, U1.D6_(PWM)
  N20: J29.pin1, U1.D11_(PWM)
  N21: J29.pin2, U1.D10_(PWM)
  N22: J29.pin3, U1.D9_(PWM)
  N23: J30.pin1, U1.A2
  N24: J30.pin2, U1.A1
  N25: J30.pin3, U1.A0
  N26: J32.pin1, U1.D13, Q5.B
  N27: J32.pin2, U1.D12, Q6.B
  N28: J33.pin1, Q2.B, U1.A5
  N29: J33.pin2, U1.A4, Q3.B
  N30: J33.pin3, U1.A3, Q4.B
  N31: J35.pin2, R10.Pin_1
  N32: J37.pin1, U1.D7, Q9.B, Q8.B
  N33: J37.pin2, U1.D8, Q7.B
  N34: Q2.C, R3.Pin_0
  N35: Q9.C, R10.Pin_0
  N36: Q3.C, R4.Pin_0
  N37: Q4.C, R5.Pin_0
  N38: Q5.C, R6.Pin_0
  N39: Q6.C, R7.Pin_0
  N40: Q7.C, R8.Pin_0
  N41: Q8.C, R9.Pin_0
