# Fritzing sketch v2 (saved by Fritzing 0.9.1b)
circuit board: 1.06514cm x 2.32572cm
circuit board: 1.55233cm x 4.39683cm
breadboards: 1

parts:
  XTAL1 = Crystal [frequency="16 Mhz" package=THT]
  C1 = Ceramic Capacitor [capacitance=100nF package="100 mil [THT, multilayer]"]
  C2 = Ceramic Capacitor [capacitance=100nF package="100 mil [THT, multilayer]"]
  J11 = female pin header, 3 pins [form="♀ (female)"]
  J12 = female pin header, 3 pins [form="♀ (female)"]
  J13 = female pin header, 3 pins [form="♀ (female)"]
  J14 = female pin header, 3 pins [form="♀ (female)"]
  J15 = female pin header, 3 pins [form="♀ (female)"]
  J16 = female pin header, 3 pins [form="♀ (female)"]
  J18 = female pin header, 3 pins [form="♀ (female)"]
  J30 = female pin header, 3 pins [form="♀ (female)"]
  J31 = female pin header, 3 pins [form="♀ (female)"]
  J33 = female pin header, 3 pins [form="♀ (female)"]
  J34 = female pin header, 2 pins [form="♀ (female)"]
  J38 = female pin header, 5 pins [form="♀ (female)"]
  U1 = atmega328 [package=dip]
  J28 = female pin header, 4 pins [form="♀ (female)"]
  J32 = female pin header, 5 pins [form="♀ (female)"]
  R1 = Resistor [tolerance=±5% resistance=220 package=THT]
  J40 = female pin header, 6 pins [form="♀ (female)"]
  J41 = female pin header, 6 pins [form="♀ (female)"]
  J42 = female pin header, 6 pins [form="♀ (female)"]
  J43 = female pin header, 6 pins [form="♀ (female)"]
  J44 = female pin header, 6 pins [form="♀ (female)"]
  J39 = female pin header, 3 pins [form="♀ (female)"]
  J45 = female pin header, 4 pins [form="♀ (female)"]
  J46 = female pin header, 1 pin [form="♀ (female)"]
  J47 = female pin header, 3 pins [form="♀ (female)"]
  J48 = female pin header, 1 pin [form="♀ (female)"]
  J49 = female pin header, 1 pin [form="♀ (female)"]

nets:
  N1: XTAL1.pin_0, C1.0, U1.XLAT2
  N2: XTAL1.pin_1, C2.0, U1.XLAT1
  N3: C1.1, C2.1, J11.pin3, J12.pin3, J13.pin3, J14.pin3, J15.pin3, J16.pin3, J34.pin2, J38.pin5, U1.GND, J40.pin1, J42.pin6, J43.pin3, J44.pin3, J39.pin1, J39.pin3, J48.pin1
  N4: J11.pin1, J12.pin1, J31.pin3, J38.pin3, U1.D4, J47.pin3
  N5: J13.pin1, J14.pin1, J31.pin2, J38.pin2, U1.D3_(PWM), J47.pin2
  N6: J15.pin1, J16.pin1, J31.pin1, J38.pin1, U1.D2, J47.pin1
  N7: J18.pin1, U1.RESET, R1.Pin_0
  N8: J18.pin2, U1.D0_(RX)
  N9: J18.pin3, U1.D1_(TX)
  N10: J30.pin1, U1.A2, J42.pin3, J43.pin4
  N11: J30.pin2, U1.A1, J42.pin4, J43.pin5
  N12: J30.pin3, U1.A0, J42.pin5, J43.pin6
  N13: J33.pin1, U1.A5
  N14: J33.pin2, U1.A4, J42.pin1, J43.pin1
  N15: J33.pin3, U1.A3, J42.pin2, J43.pin2
  N16: J34.pin1, U1.VCC, U1.AVCC, U1.AREF, R1.Pin_1, J41.pin1, J41.pin4, J39.pin2, J46.pin1, J49.pin1
  N17: U1.D5_(PWM), J28.pin1, J41.pin2, J45.pin1
  N18: U1.D6_(PWM), J28.pin2, J41.pin3, J45.pin2
  N19: U1.D7, J28.pin3, J41.pin5, J45.pin3
  N20: U1.D8, J28.pin4, J41.pin6, J45.pin4
  N21: U1.D9_(PWM), J32.pin5, J40.pin6, J44.pin6
  N22: U1.D10_(PWM), J32.pin4, J40.pin5, J44.pin5
  N23: U1.D11_(PWM), J32.pin3, J40.pin4, J44.pin4
  N24: U1.D12, J32.pin2, J40.pin3, J44.pin2
  N25: U1.D13, J32.pin1, J40.pin2, J44.pin1
