# Fritzing sketch FastClick (saved by Fritzing 0.9.1b)
breadboards: 1

parts:
  Part1 = Arduino Uno (Rev3)
  S1 = Pushbutton [package="[THT]"]
  R2 = Resistor [tolerance=±5% resistance=1k package=THT]
  LED1 = LED - 5mm [color="Red (633nm)" package="5 mm [THT]"]
  R1 = Resistor [tolerance=±5% resistance=220 package=THT]

nets:
  N1: Part1.GND, R2.Pin_1, LED1.cathode
  N2: Part1.D3_PWM, R1.Pin_1
  N3: Part1.D7, S1.Pin_3, S1.Pin_4, R2.Pin_0
  N4: Part1.5V, S1.Pin_1, S1.Pin_2
  N5: LED1.anode, R1.Pin_0
