# Fritzing sketch Geocache Computer (saved by Fritzing 0.9.1b)
circuit board: 1.5055cm x 4.06689cm
circuit board: 6.10783cm x 4.06442cm
breadboards: 1

parts:
  IC1 = IC, DIP package, 16 pins [chip_label=IC]
  R2 = Resistor [tolerance=±5% resistance=220 package=THT]
  R3 = Trimmer Potentiometer [maximum_resistance=10kΩ package=THT]
  R4 = Resistor [tolerance=±5% resistance=1k package=THT]
  J1 = female pin header, 3 pins [form="♀ (female)"]
  J2 = female pin header, 3 pins [form="♀ (female)"]
  J3 = female pin header, 3 pins [form="♀ (female)"]
  J4 = female pin header, 3 pins [form="♀ (female)"]
  J6 = female pin header, 3 pins [form="♀ (female)"]  # not connected
  J5 = female pin header, 3 pins [form="♀ (female)"]
  J7 = female pin header, 3 pins [form="♀ (female)"]  # not connected
  J8 = female pin header, 3 pins [form="♀ (female)"]
  J9 = female pin header, 3 pins [form="♀ (female)"]
  J10 = female pin header, 3 pins [form="♀ (female)"]
  B1 = female pin header, 3 pins [form="♀ (female)"]
  J12 = female pin header, 3 pins [form="♀ (female)"]
  J13 = female pin header, 3 pins [form="♀ (female)"]
  J14 = female pin header, 3 pins [form="♀ (female)"]
  J15 = female pin header, 3 pins [form="♀ (female)"]
  J16 = female pin header, 3 pins [form="♀ (female)"]
  J17 = female pin header, 3 pins [form="♀ (female)"]
  J18 = female pin header, 3 pins [form="♀ (female)"]
  J19 = female pin header, 3 pins [form="♀ (female)"]  # not connected
  J20 = female pin header, 3 pins [form="♀ (female)"]
  J21 = female pin header, 3 pins [form="♀ (female)"]
  J22 = female pin header, 3 pins [form="♀ (female)"]
  J23 = female pin header, 3 pins [form="♀ (female)"]  # not connected
  J24 = female pin header, 3 pins [form="♀ (female)"]
  LCD1 = LCD screen
  J25 = female pin header, 24 pins [form="♀ (female)"]  # not connected
  J28 = female pin header, 3 pins [form="♀ (female)"]  # not connected
  J31 = female pin header, 3 pins [form="♀ (female)"]
  J32 = female pin header, 3 pins [form="♀ (female)"]
  J29 = female pin header, 3 pins [form="♀ (female)"]
  U1 = atmega168 [package=dip]
  J34 = female pin header, 9 pins [form="♀ (female)"]
  LCD2 = LCD screen  # not connected
  R5 = Resistor [tolerance=±5% resistance=1k package=THT]
  R6 = Resistor [tolerance=±5% resistance=1k package=THT]
  XTAL1 = Crystal [frequency="16 Mhz" package=THT]
  J33 = female pin header, 9 pins [form="♀ (female)"]
  C1 = Ceramic Capacitor [capacitance=100nF package="100 mil [THT, multilayer]"]
  C2 = Ceramic Capacitor [capacitance=100nF package="100 mil [THT, multilayer]"]

nets (from the pcb view):
  N1: IC1.pin1, J5.pin1
  N2: IC1.pin2, J22.pin1
  N3: IC1.pin3, J13.pin1
  N4: IC1.pin4, J20.pin1
  N5: IC1.pin5, J18.pin1
  N6: IC1.pin6, J15.pin1
  N7: IC1.pin7, J8.pin1, J24.pin1
  N8: IC1.pin8, J32.pin1, U1.GND#7, R5.Pin_0, R6.Pin_0, C1.0, C2.1
  N9: IC1.pin9, J4.pin1, J10.pin1
  N10: IC1.pin10, J12.pin1
  N11: IC1.pin11, IC1.pin15
  N12: IC1.pin13, J31.pin1, J29.pin1
  N13: IC1.pin14, U1.D3_(PWM)
  N14: IC1.pin16, R4.Pin_1, U1.VCC
  N15: R2.Pin_0, LCD1.LED+
  N16: R2.Pin_1, R3.leg1, LCD1.VDD, J34.pin2
  N17: R3.wiper, LCD1.V0
  N18: R3.leg2, LCD1.VSS, LCD1.R/W, LCD1.LED-, J34.pin1
  N19: R4.Pin_0, U1.RESET
  N20: J1.pin1, B1.pin1
  N21: J1.pin3, J4.pin3
  N22: J2.pin3, U1.D8, R6.Pin_1
  N23: J3.pin3, J24.pin3
  N24: J5.pin3, J8.pin3, J9.pin3, J14.pin3, J16.pin3, J20.pin3
  N25: J10.pin3, B1.pin3
  N26: J12.pin3, U1.D7, R5.Pin_1
  N27: J13.pin3, J21.pin3
  N28: J15.pin3, J17.pin3
  N29: LCD1.RS, J34.pin9
  N30: LCD1.E, J34.pin8
  N31: LCD1.DB4, J34.pin7
  N32: LCD1.DB5, J34.pin6
  N33: LCD1.DB6, J34.pin5
  N34: LCD1.DB7, J34.pin4
  N35: J31.pin3, U1.D4
  N36: J29.pin3, U1.D2
  N37: U1.XLAT1, XTAL1.pin_1, C2.0
  N38: U1.XLAT2, XTAL1.pin_0, C1.1
  N39: U1.D5_(PWM), J33.pin8
  N40: U1.D6_(PWM), J33.pin9
  N41: U1.D9_(PWM), J33.pin7
  N42: U1.D10_(PWM), J33.pin6
  N43: U1.D11_(PWM), J33.pin5
  N44: U1.D12, J33.pin4
  N45: U1.D13, J33.pin3
  N46: U1.AVCC, U1.AREF, J33.pin2
  N47: U1.GND#21, J33.pin1
