# Fritzing sketch ledcube (saved by Fritzing 0.9.1b)
circuit board: 5.65cm x 5.65cm
breadboards: 1

parts:
  LED21 = LED - 5mm [color="Red (633nm)" package="5 mm [THT]"]
  U1 = atmega168 [package=dip]
  J1 = female pin header, 1 pin [form="♀ (female)"]
  J2 = female pin header, 1 pin [form="♀ (female)"]
  J3 = female pin header, 1 pin [form="♀ (female)"]
  J4 = female pin header, 1 pin [form="♀ (female)"]
  J5 = female pin header, 1 pin [form="♀ (female)"]
  J6 = female pin header, 1 pin [form="♀ (female)"]
  J7 = female pin header, 1 pin [form="♀ (female)"]
  J8 = female pin header, 1 pin [form="♀ (female)"]
  J9 = female pin header, 1 pin [form="♀ (female)"]
  XTAL1 = Crystal [frequency="16 Mhz" package=THT]
  C1 = Ceramic Capacitor [capacitance=100nF package="100 mil [THT, multilayer]"]
  C2 = Ceramic Capacitor [capacitance=100nF package="100 mil [THT, multilayer]"]
  J14 = female pin header, 2 pins [form="♀ (female)"]
  J12 = female pin header, 7 pins [form="♀ (female)"]
  J11 = female pin header, 3 pins [form="♀ (female)"]
  Q3 = NPN-Transistor [package="TO92 [THT]"]
  R2 = Resistor [tolerance=±5% resistance=1k package=THT]
  R3 = Resistor [tolerance=±5% resistance=1k package=THT]
  R7 = Resistor [tolerance=±5% resistance=220 package=THT]
  Q2 = NPN-Transistor [package="TO92 [THT]"]
  Q1 = NPN-Transistor [package="TO92 [THT]"]
  R4 = Resistor [tolerance=±5% resistance=1k package=THT]
  R5 = Resistor [tolerance=±5% resistance=220 package=THT]
  R6 = Resistor [tolerance=±5% resistance=220 package=THT]
  J13 = female pin header, 2 pins [form="♀ (female)"]
  J15 = female pin header, 2 pins [form="♀ (female)"]
  J16 = female pin header, 2 pins [form="♀ (female)"]
  LED27 = LED - 3mm [color="Green (555nm)" package="3 mm [THT]"]
  LED28 = LED - 3mm [color="Green (555nm)" package="3 mm [THT]"]
  R8 = Resistor [tolerance=±5% resistance=1k package=THT]
  R1 = Resistor [tolerance=±5% resistance=220 package="0805 [SMD]"]
  Pad1 = Pad [width=1.19597438983842 height=12.2415463004414 connect=center]  # not connected
  Pad2 = Pad [width=1.19595691402635 height=33.5001365681243 connect=center]  # not connected
  VCC1 = 4 x AAA Battery Mount  # not connected

nets:
  N1: LED21.cathode, R6.Pin_1
  N2: U1.RESET, J11.pin3, R1.Pin_0
  N3: U1.D0_(RX), J11.pin2
  N4: U1.D1_(TX), J11.pin1
  N5: U1.D2, R2.Pin_1
  N6: U1.D3_(PWM), R3.Pin_1
  N7: U1.D4, R4.Pin_1
  N8: U1.VCC, U1.AVCC, U1.AREF, J14.pin1, J15.pin2, R1.Pin_1
  N9: U1.GND, C1.1, C2.1, J14.pin2, J12.pin1, J15.pin1, J16.pin1, J16.pin2, LED27.cathode
  N10: U1.XLAT1, XTAL1.pin_0, C2.0
  N11: U1.XLAT2, XTAL1.pin_1, C1.0
  N12: U1.D5_(PWM), J3.pin1, LED28.anode
  N13: U1.D6_(PWM), J4.pin1
  N14: U1.D7, J5.pin1
  N15: U1.D8, J2.pin1
  N16: U1.D9_(PWM), J1.pin1
  N17: U1.D10_(PWM), J9.pin1
  N18: U1.D11_(PWM), J8.pin1
  N19: U1.D12, J6.pin1
  N20: U1.D13, J7.pin1
  N21: U1.A0, J12.pin2
  N22: U1.A1, J12.pin3
  N23: U1.A2, J12.pin4
  N24: U1.A3, J12.pin5
  N25: U1.A4, J12.pin6
  N26: U1.A5, J12.pin7
  N27: Q3.E, Q2.E, Q1.E, R8.Pin_1
  N28: Q3.B, R3.Pin_0
  N29: Q3.C, R6.Pin_0
  N30: R2.Pin_0, Q2.B, LED27.anode
  N31: R7.Pin_0, Q2.C
  N32: R7.Pin_1, J13.pin1
  N33: Q1.B, R4.Pin_0
  N34: Q1.C, R5.Pin_0
  N35: R5.Pin_1, J13.pin2
  N36: LED28.cathode, R8.Pin_0

notes:
  .
  jasonamri
