# Fritzing sketch rele (saved by Fritzing 0.9.1b)
circuit board: 10cm x 6cm
circuit board: 5.69611cm x 2.698cm
breadboards: 1

parts:
  LCD1 = LCD screen
  R2 = Trimmer Potentiometer [maximum_resistance=10kΩ package=THT]
  R3 = Resistor [tolerance=±5% resistance=220 package=THT]

nets:
  N1: LCD1.VSS, LCD1.R/W, LCD1.LED-, R2.leg1
  N2: LCD1.VDD, R2.leg2
  N3: LCD1.V0, R2.wiper
  N4: LCD1.LED+, R3.Pin_0
