# Fritzing sketch buttonmatrix (saved by Fritzing 0.9.1b)
circuit board: 3.44002cm x 5.51877cm
breadboards: 1

parts:
  S1 = Pushbutton [package="[THT]"]
  S2 = Pushbutton [package="[THT]"]
  S3 = Pushbutton [package="[THT]"]
  S4 = Pushbutton [package="[THT]"]
  S5 = Pushbutton [package="[THT]"]
  S6 = Pushbutton [package="[THT]"]
  S7 = Pushbutton [package="[THT]"]
  S8 = Pushbutton [package="[THT]"]
  S9 = Pushbutton [package="[THT]"]
  S10 = Pushbutton [package="[THT]"]
  S11 = Pushbutton [package="[THT]"]
  S12 = Pushbutton [package="[THT]"]
  J1 = female pin header, 3 pins [form="♀ (female)"]
  R1 = Resistor [tolerance=±5% resistance=10k package=THT]
  R2 = Resistor [tolerance=±5% resistance=1k package=THT]
  R3 = Resistor [tolerance=±5% resistance=1k package=THT]
  R4 = Resistor [tolerance=±5% resistance=1k package=THT]
  R5 = Resistor [tolerance=±5% resistance=1k package=THT]
  R6 = Resistor [tolerance=±5% resistance=1k package=THT]
  R7 = Resistor [tolerance=±5% resistance=1k package=THT]
  R8 = Resistor [tolerance=±5% resistance=1k package=THT]
  R9 = Resistor [tolerance=±5% resistance=1k package=THT]
  R10 = Resistor [tolerance=±5% resistance=1k package=THT]
  R11 = Resistor [tolerance=±5% resistance=1k package=THT]
  R12 = Resistor [tolerance=±5% resistance=1k package=THT]
  R13 = Resistor [tolerance=±5% resistance=1k package=THT]

nets:
  N1: S1.Pin_1, S1.Pin_2, S2.Pin_1, S2.Pin_2, S3.Pin_1, S3.Pin_2, S4.Pin_1, S4.Pin_2, S5.Pin_2, S6.Pin_1, S6.Pin_2, S7.Pin_1, S7.Pin_2, S8.Pin_1, S8.Pin_2, S9.Pin_2, S10.Pin_1, S10.Pin_2, S11.Pin_1, S11.Pin_2, S12.Pin_2, J1.pin2, R1.Pin_1
  N2: S1.Pin_3, S1.Pin_4, R10.Pin_0, R11.Pin_1
  N3: S2.Pin_3, S2.Pin_4, R12.Pin_0, R13.Pin_1
  N4: S3.Pin_3, S3.Pin_4, R3.Pin_0, R7.Pin_1
  N5: S4.Pin_3, S4.Pin_4, R9.Pin_0, R10.Pin_1
  N6: S5.Pin_3, S5.Pin_4, R11.Pin_0, R12.Pin_1
  N7: S6.Pin_3, S6.Pin_4, R2.Pin_0, R3.Pin_1
  N8: S7.Pin_3, S7.Pin_4, R13.Pin_0
  N9: S8.Pin_3, S8.Pin_4, R2.Pin_1, R4.Pin_0
  N10: S9.Pin_3, S9.Pin_4, R5.Pin_1, R7.Pin_0
  N11: S10.Pin_3, S10.Pin_4, R5.Pin_0, R6.Pin_1
  N12: S11.Pin_3, S11.Pin_4, R6.Pin_0, R8.Pin_1
  N13: S12.Pin_3, S12.Pin_4, R8.Pin_0, R9.Pin_1
  N14: J1.pin1, R4.Pin_1
  N15: J1.pin3, R1.Pin_0
