# Fritzing sketch rgbled Photon (saved by Fritzing 0.9.1b)
circuit board: 3.84186cm x 3.08119cm
breadboards: 1

parts:
  Q4 = Basic FET N-Channel [package="TO220 [THT]"]
  Q5 = Basic FET N-Channel [package="TO220 [THT]"]
  Q6 = Basic FET N-Channel [package="TO220 [THT]"]
  U2 = Voltage Regulator - 3.3V [package="TO220 [THT]"]
  J3 = female pin header, 2 pins [form="♀ (female)"]
  J4 = female pin header, 4 pins [form="♀ (female)"]
  Part1 = Photon

nets:
  N1: Q4.gate, Part1.A4
  GND: Q4.drain, Q5.drain, Q6.drain, U2.GND, J3.pin2, Part1.GND
  N2: Q4.source, J4.pin4
  N3: Q5.gate, Part1.A5
  N4: Q5.source, J4.pin3
  N5: Q6.gate, Part1.RX
  N6: Q6.source, J4.pin2
  12V: U2.input_voltage, J3.pin1, J4.pin1
  N7: U2.output_voltage, Part1.3V3
