# Fritzing sketch rgbled copy (saved by Fritzing 0.9.1b)
circuit board: 5.05258cm x 2.64163cm
breadboards: 1

parts:
  R1 = Resistor [tolerance=±5% resistance=10k package=THT]
  C1 = Ceramic Capacitor [capacitance=100nF package="100 mil [THT, multilayer]"]
  C2 = Ceramic Capacitor [capacitance=100nF package="100 mil [THT, multilayer]"]
  Q1 = Basic FET N-Channel [package="TO220 [THT]"]
  Q2 = Basic FET N-Channel [package="TO220 [THT]"]
  Q3 = Basic FET N-Channel [package="TO220 [THT]"]
  U2 = Voltage Regulator - 5V [package="TO220 [THT]"]
  J1 = female pin header, 3 pins [form="♀ (female)"]
  J2 = female pin header, 4 pins [form="♀ (female)"]
  U1 = atmega328 [package=dip]
  J3 = female pin header, 2 pins [form="♀ (female)"]
  XTAL1 = Crystal [frequency="16 Mhz" package=THT]

nets:
  N1: R1.Pin_0, U1.RESET
  N2: R1.Pin_1, U2.output_voltage, J1.pin2, U1.VCC, U1.AVCC, U1.AREF
  N3: C1.0, U1.XLAT2, XTAL1.pin_1
  GND: C1.1, C2.1, Q1.drain, Q2.drain, Q3.drain, U2.GND, J1.pin1, U1.GND, J3.pin2
  N4: C2.0, U1.XLAT1, XTAL1.pin_0
  N5: Q1.gate, U1.D6_(PWM)
  N6: Q1.source, J2.pin4
  N7: Q2.gate, U1.D5_(PWM)
  N8: Q2.source, J2.pin2
  N9: Q3.gate, U1.D3_(PWM)
  N10: Q3.source, J2.pin3
  12V: U2.input_voltage, J2.pin1, J3.pin1
  N11: J1.pin3, U1.D4

// code stored in the sketch: Untitled.ino
#include <IRremote.h>
int state = 0;
int redValue = 0;
int greenValue = 0;
int blueValue = 0;

IRrecv irrecv(12);
decode_results results;

void setup() {
  irrecv.enableIRIn();
  pinMode(9, OUTPUT);
  pinMode(10, OUTPUT);
  pinMode(6, OUTPUT);
  Serial.begin(9600);
  
}

void loop() {
if (irrecv.decode(&results)) {

  
  if (results.value==0xE0E016E9){ //Code to turn the LED ON/OFF
    if(state==0){ // if the LED was turned off, then we turn it on 
      digitalWrite(9,HIGH);
      digitalWrite(10,HIGH);
      digitalWrite(6,HIGH);
      analogWrite(9,redValue);
      analogWrite(10,blueValue);
      analogWrite(6,greenValue);
      state=1;
    }
    else{
      digitalWrite(9,LOW);
      digitalWrite(10,LOW);
      digitalWrite(6,LOW);
      state=0; 
    }
    delay(250);
  }
    
    
    
    
  if (results.value==0xE0E0A25D && state==1){ //Code to increase the brightness
    if(redValue>249){ 
      analogWrite(9,redValue);
    }
    else{
    redValue=redValue+25;
    analogWrite(9,redValue);
  }
delay(250);
}

  if (results.value==0xE0E0926D && state==1){ //Code to decrease the brightness
    if(redValue<25){ 
      analogWrite(9,redValue);
    }
    else{
    redValue=redValue-25;
    analogWrite(9,redValue);
  }
delay(250);
}
  
  
  
  
  
  
    if (results.value==0xE0E052AD && state==1){ //Code to increase the brightness
    if(blueValue>249){ 
      analogWrite(10,blueValue);
    }
    else{
    blueValue=blueValue+25;
    analogWrite(10,blueValue);
  }
delay(250);
}

  if (results.value==0xE0E0E21D && state==1){ //Code to decrease the brightness
    if(blueValue<25){ 
      analogWrite(10,blueValue);
    }
    else{
    blueValue=blueValue-25;
    analogWrite(10,blueValue);
  }
delay(250);
}



    if (results.value==0xE0E012ED && state==1){ //Code to increase the brightness
    if(greenValue>249){ 
      analogWrite(6,greenValue);
    }
    else{
    greenValue=greenValue+25;
    analogWrite(6,greenValue);
  }
delay(250);
}

  if (results.value==0xE0E0629D && state==1){ //Code to decrease the brightness
    if(greenValue<25){ 
      analogWrite(6,greenValue);
    }
    else{
    greenValue=greenValue-25;
    analogWrite(6,greenValue);
  }
delay(250);
}





  
  irrecv.resume();
}
}
