# Fritzing sketch rgbled (saved by Fritzing 0.9.1b)
circuit board: 8.46667cm x 5.64444cm
breadboards: 1

parts:
  S1 = Pushbutton [package="[THT]"]
  R1 = Resistor [tolerance=±5% resistance=10k package=THT]
  C1 = Ceramic Capacitor [capacitance=100nF package="100 mil [THT, multilayer]"]
  C2 = Ceramic Capacitor [capacitance=100nF package="100 mil [THT, multilayer]"]
  XTAL1 = Crystal [frequency="16 Mhz" package=THT]
  Q1 = Basic FET N-Channel [package="TO220 [THT]"]
  Q2 = Basic FET N-Channel [package="TO220 [THT]"]
  Q3 = Basic FET N-Channel [package="TO220 [THT]"]
  U2 = Voltage Regulator - 5V [package="TO220 [THT]"]
  J1 = female pin header, 3 pins [form="♀ (female)"]
  J2 = female pin header, 4 pins [form="♀ (female)"]
  U1 = atmega328 [package=dip]
  J3 = female pin header, 2 pins [form="♀ (female)"]

nets (from the schematic view):
  N1: S1.Pin_1, S1.Pin_2, R1.Pin_0, U1.RESET
  GND: S1.Pin_3, S1.Pin_4, C1.1, C2.1, Q1.drain, Q2.drain, Q3.drain, U2.GND, J1.pin1, U1.GND, J3.pin2
  N2: R1.Pin_1, U2.output_voltage, J1.pin2, U1.VCC, U1.AVCC, U1.AREF
  N3: C1.0, XTAL1.pin_1, U1.XLAT2
  N4: C2.0, XTAL1.pin_0, U1.XLAT1
  N5: Q1.gate, U1.D6_(PWM)
  N6: Q1.source, J2.pin4
  N7: Q2.gate, U1.D5_(PWM)
  N8: Q2.source, J2.pin3
  N9: Q3.gate, U1.D3_(PWM)
  N10: Q3.source, J2.pin2
  12V: U2.input_voltage, J2.pin1, J3.pin1
  N11: J1.pin3, U1.D4
