# Fritzing sketch v1 (saved by Fritzing 0.9.1b)
circuit board: 8.46667cm x 5.64444cm
breadboards: 1

parts:
  U1 = atmega328 [package=dip]
  XTAL1 = Crystal [frequency="16 Mhz" package=THT]
  C1 = Ceramic Capacitor [capacitance=22nF package="100 mil [THT, multilayer]"]
  C2 = Ceramic Capacitor [capacitance=22nF package="100 mil [THT, multilayer]"]
  J1 = male pin header, 3 pins [form="♂ (male)"]
  J2 = female pin header, 10 pins [form="♀ (female)"]
  R1 = Resistor [tolerance=±5% resistance=220 package=THT]
  R2 = Resistor [tolerance=±5% resistance=220 package=THT]
  R3 = Resistor [tolerance=±5% resistance=220 package=THT]
  R4 = Resistor [tolerance=±5% resistance=220 package=THT]
  R5 = Resistor [tolerance=±5% resistance=220 package=THT]
  R6 = Resistor [tolerance=±5% resistance=220 package=THT]
  R7 = Resistor [tolerance=±5% resistance=220 package=THT]
  R8 = Resistor [tolerance=±5% resistance=220 package=THT]
  R9 = Resistor [tolerance=±5% resistance=220 package=THT]
  R10 = Resistor [tolerance=±5% resistance=1k package=THT]

nets:
  N1: U1.RESET, R10.Pin_1
  N2: U1.D4, J1.pin1
  N3: U1.VCC, U1.AVCC, U1.AREF, J1.pin2, R10.Pin_0
  N4: U1.GND, C1.1, C2.1, J1.pin3, J2.pin1
  N5: U1.XLAT1, XTAL1.pin_1, C2.0
  N6: U1.XLAT2, XTAL1.pin_0, C1.0
  N7: U1.D5_(PWM), R1.Pin_1
  N8: U1.D6_(PWM), R2.Pin_1
  N9: U1.D7, R3.Pin_1
  N10: U1.D8, R4.Pin_1
  N11: U1.D9_(PWM), R5.Pin_1
  N12: U1.D10_(PWM), R6.Pin_1
  N13: U1.D11_(PWM), R7.Pin_1
  N14: U1.D12, R8.Pin_1
  N15: U1.D13, R9.Pin_1
  N16: J2.pin2, R9.Pin_0
  N17: J2.pin3, R8.Pin_0
  N18: J2.pin4, R7.Pin_0
  N19: J2.pin5, R6.Pin_0
  N20: J2.pin6, R5.Pin_0
  N21: J2.pin7, R4.Pin_0
  N22: J2.pin8, R3.Pin_0
  N23: J2.pin9, R2.Pin_0
  N24: J2.pin10, R1.Pin_0
