# Fritzing sketch v2 (saved by Fritzing 0.9.1b)
circuit board: 6.21192cm x 3.70109cm
breadboards: 1

parts:
  R2 = Resistor [tolerance=±5% resistance=220 package=THT]
  R3 = Resistor [tolerance=±5% resistance=220 package=THT]
  R4 = Resistor [tolerance=±5% resistance=220 package=THT]
  R5 = Resistor [tolerance=±5% resistance=220 package=THT]
  R6 = Resistor [tolerance=±5% resistance=220 package=THT]
  R7 = Resistor [tolerance=±5% resistance=220 package=THT]
  R8 = Resistor [tolerance=±5% resistance=220 package=THT]
  R9 = Resistor [tolerance=±5% resistance=220 package=THT]
  J1 = female pin header, 3 pins [form="♀ (female)"]
  Q1 = NPN-Transistor [package="TO92 [THT]"]
  Q2 = NPN-Transistor [package="TO92 [THT]"]
  Q3 = NPN-Transistor [package="TO92 [THT]"]
  Q4 = NPN-Transistor [package="TO92 [THT]"]
  Q5 = NPN-Transistor [package="TO92 [THT]"]
  Q6 = NPN-Transistor [package="TO92 [THT]"]
  Q7 = NPN-Transistor [package="TO92 [THT]"]
  Q8 = NPN-Transistor [package="TO92 [THT]"]
  J2 = female pin header, 16 pins [form="♀ (female)"]
  J3 = female pin header, 12 pins [form="♀ (female)"]

nets:
  N1: R2.Pin_0, Q1.C
  N2: R2.Pin_1, J2.pin1
  N3: R3.Pin_0, Q2.C
  N4: R3.Pin_1, J2.pin2
  N5: R4.Pin_0, Q3.C
  N6: R4.Pin_1, J2.pin3
  N7: R5.Pin_0, Q4.C
  N8: R5.Pin_1, J2.pin4
  N9: R6.Pin_0, Q5.C
  N10: R6.Pin_1, J2.pin5
  N11: R7.Pin_0, Q6.C
  N12: R7.Pin_1, J2.pin6
  N13: R8.Pin_0, Q7.C
  N14: R8.Pin_1, J2.pin7
  N15: R9.Pin_0, Q8.C
  N16: R9.Pin_1, J2.pin8
  N17: J1.pin1, J3.pin10
  N18: J1.pin2, Q1.E, Q2.E, Q3.E, Q4.E, Q5.E, Q6.E, Q7.E, Q8.E, J3.pin12
  N19: J1.pin3, J2.pin9
  N20: Q1.B, J3.pin1
  N21: Q2.B, J3.pin2
  N22: Q3.B, J3.pin3
  N23: Q4.B, J3.pin4
  N24: Q5.B, J3.pin5
  N25: Q6.B, J3.pin6
  N26: Q7.B, J3.pin7
  N27: Q8.B, J3.pin8
