# Fritzing sketch turkey computer copy (saved by Fritzing 0.9.1b)
circuit board: 4.62837cm x 6.1317cm
circuit board: 8.41289cm x 3.7cm
circuit board: 5.2cm x 3.8cm
breadboards: 1

parts:
  IC1 = IC, DIP package, 16 pins [chip_label=IC]
  VCC1 = Battery
  U1 = atmega168 [package=dip]
  R2 = Resistor [tolerance=±5% resistance=220 package=THT]
  R3 = Trimmer Potentiometer [maximum_resistance=10kΩ package=THT]
  R4 = Resistor [tolerance=±5% resistance=1k package=THT]
  J1 = female pin header, 3 pins [form="♀ (female)"]
  J2 = female pin header, 3 pins [form="♀ (female)"]
  J3 = female pin header, 3 pins [form="♀ (female)"]
  J4 = female pin header, 3 pins [form="♀ (female)"]
  J6 = female pin header, 3 pins [form="♀ (female)"]
  J5 = female pin header, 3 pins [form="♀ (female)"]
  J7 = female pin header, 3 pins [form="♀ (female)"]
  J8 = female pin header, 3 pins [form="♀ (female)"]
  J9 = female pin header, 3 pins [form="♀ (female)"]
  J10 = female pin header, 3 pins [form="♀ (female)"]
  B1 = female pin header, 3 pins [form="♀ (female)"]
  J12 = female pin header, 3 pins [form="♀ (female)"]
  J13 = female pin header, 3 pins [form="♀ (female)"]
  J14 = female pin header, 3 pins [form="♀ (female)"]
  J15 = female pin header, 3 pins [form="♀ (female)"]
  J16 = female pin header, 3 pins [form="♀ (female)"]
  J17 = female pin header, 3 pins [form="♀ (female)"]
  J18 = female pin header, 3 pins [form="♀ (female)"]
  J19 = female pin header, 3 pins [form="♀ (female)"]
  J20 = female pin header, 3 pins [form="♀ (female)"]
  J21 = female pin header, 3 pins [form="♀ (female)"]
  J22 = female pin header, 3 pins [form="♀ (female)"]
  J23 = female pin header, 3 pins [form="♀ (female)"]
  J24 = female pin header, 3 pins [form="♀ (female)"]
  J25 = female pin header, 18 pins [form="♀ (female)"]  # not connected
  J26 = female pin header, 18 pins [form="♀ (female)"]  # not connected
  J27 = female pin header, 14 pins [form="♀ (female)"]  # not connected

nets:
  N1: IC1.pin1, J3.pin1, J4.pin1, J9.pin1, J10.pin1
  N2: IC1.pin2, J6.pin1, J5.pin1
  N3: IC1.pin3, J7.pin1, J8.pin1
  N4: IC1.pin4, J1.pin1, J2.pin1, B1.pin1, J12.pin1
  N5: IC1.pin5, J15.pin1, J16.pin1
  N6: IC1.pin6, J19.pin1, J20.pin1
  N7: IC1.pin7, J17.pin1, J18.pin1
  N8: IC1.pin8, IC1.pin13, IC1.pin15, VCC1.-, U1.GND
  N9: IC1.pin9, J13.pin1, J14.pin1
  N10: IC1.pin10, J23.pin1, J24.pin1
  N11: IC1.pin11, J21.pin1, J22.pin1
  N12: IC1.pin14, U1.D2
  N13: IC1.pin16, VCC1.+, U1.VCC, U1.AVCC, U1.AREF, R2.Pin_1, R3.leg2, R4.Pin_1
  N14: U1.RESET, R4.Pin_0
  N15: U1.D8, J1.pin3, J2.pin3, J3.pin3, J4.pin3
  N16: U1.D9_(PWM), J6.pin3, J5.pin3, J7.pin3, J8.pin3, J9.pin3, J10.pin3, B1.pin3, J12.pin3, J13.pin3, J14.pin3, J15.pin3, J16.pin3, J17.pin3, J18.pin3, J19.pin3, J20.pin3, J21.pin3, J22.pin3, J23.pin3, J24.pin3
